// Logisim project 2021113411_표수현_HW3.circ as structural Verilog: 12 circuits, main circuit main
module main (
  input  A0,
  input  A1,
  input  A2,
  input  A3,
  input  B0,
  input  B1,
  input  B2,
  input  B3,
  input  OP0,
  input  OP1,
  input  OP2,
  output C0,
  output C1,
  output C2,
  output C3
);

  wire _4_bit_adder_s0, _4_bit_adder_s1, _4_bit_adder_s2, _4_bit_adder_s3, _4_bit_and_c0, _4_bit_and_c1,
       _4_bit_and_c2, _4_bit_and_c3, _4_bit_not_a_prime_0, _4_bit_not_a_prime_1, _4_bit_not_a_prime_2,
       _4_bit_not_a_prime_3, _4_bit_or_c0, _4_bit_or_c1, _4_bit_or_c2, _4_bit_or_c3, _4_bit_substracter_d0,
       _4_bit_substracter_d1, _4_bit_substracter_d2, _4_bit_substracter_d3, _4_bit_xor_c0, _4_bit_xor_c1,
       _4_bit_xor_c2, _4_bit_xor_c3;

  _4_bit_adder _4_bit_adder (
    .A0(A0), .A1(A1), .A2(A2), .A3(A3), .B0(B0), .B1(B1), .B2(B2), .B3(B3), .S0(_4_bit_adder_s0),
    .S1(_4_bit_adder_s1), .S2(_4_bit_adder_s2), .S3(_4_bit_adder_s3));
  _4_bit_substracter _4_bit_substracter (
    .A0(A0), .A1(A1), .A2(A2), .A3(A3), .B0(B0), .B1(B1), .B2(B2), .B3(B3), .D0(_4_bit_substracter_d0),
    .D1(_4_bit_substracter_d1), .D2(_4_bit_substracter_d2), .D3(_4_bit_substracter_d3));
  _4_bit_and _4_bit_and (
    .A0(A0), .A1(A1), .A2(A2), .A3(A3), .B0(B0), .B1(B1), .B2(B2), .B3(B3), .C0(_4_bit_and_c0),
    .C1(_4_bit_and_c1), .C2(_4_bit_and_c2), .C3(_4_bit_and_c3));
  _4_bit_or _4_bit_or (
    .A0(A0), .A1(A1), .A2(A2), .A3(A3), .B0(B0), .B1(B1), .B2(B2), .B3(B3), .C0(_4_bit_or_c0),
    .C1(_4_bit_or_c1), .C2(_4_bit_or_c2), .C3(_4_bit_or_c3));
  _4_bit_xor _4_bit_xor (
    .A0(A0), .A1(A1), .A2(A2), .A3(A3), .B0(B0), .B1(B1), .B2(B2), .B3(B3), .C0(_4_bit_xor_c0),
    .C1(_4_bit_xor_c1), .C2(_4_bit_xor_c2), .C3(_4_bit_xor_c3));
  _4_bit_not _4_bit_not (
    .A0(A0), .A1(A1), .A2(A2), .A3(A3), .A_prime_0(_4_bit_not_a_prime_0), .A_prime_1(_4_bit_not_a_prime_1),
    .A_prime_2(_4_bit_not_a_prime_2), .A_prime_3(_4_bit_not_a_prime_3));
  _8_to_1_MUX _8_to_1_MUX (
    .I0(_4_bit_adder_s0), .I1(_4_bit_substracter_d0), .I2(_4_bit_and_c0), .I3(_4_bit_or_c0),
    .I4(_4_bit_xor_c0), .I5(_4_bit_not_a_prime_0), .I6(1'b0), .I7(1'b0), .OP0(OP0), .OP1(OP1), .OP3(OP2),
    .Z(C0));
  _8_to_1_MUX _8_to_1_MUX_2 (
    .I0(_4_bit_adder_s1), .I1(_4_bit_substracter_d1), .I2(_4_bit_and_c1), .I3(_4_bit_or_c1),
    .I4(_4_bit_xor_c1), .I5(_4_bit_not_a_prime_1), .I6(1'b0), .I7(1'b0), .OP0(OP0), .OP1(OP1), .OP3(OP2),
    .Z(C1));
  _8_to_1_MUX _8_to_1_MUX_3 (
    .I0(_4_bit_adder_s2), .I1(_4_bit_substracter_d2), .I2(_4_bit_and_c2), .I3(_4_bit_or_c2),
    .I4(_4_bit_xor_c2), .I5(_4_bit_not_a_prime_2), .I6(1'b0), .I7(1'b0), .OP0(OP0), .OP1(OP1), .OP3(OP2),
    .Z(C2));
  _8_to_1_MUX _8_to_1_MUX_4 (
    .I0(_4_bit_adder_s3), .I1(_4_bit_substracter_d3), .I2(_4_bit_and_c3), .I3(_4_bit_or_c3),
    .I4(_4_bit_xor_c3), .I5(_4_bit_not_a_prime_3), .I6(1'b0), .I7(1'b0), .OP0(OP0), .OP1(OP1), .OP3(OP2),
    .Z(C3));
endmodule

module _1_bit_half_adder (
  input  X,
  input  Y,
  output Sum,
  output Cout
);

  xor xor_1 (Sum, X, Y);
  and and_1 (Cout, X, Y);
endmodule

module _1_bit_full_adder (
  input  X,
  input  Y,
  input  Cin,
  output Sum,
  output Cout
);

  wire n1_bit_half_adder_1_cout, n1_bit_half_adder_1_sum, n1_bit_half_adder_2_cout;

  _1_bit_half_adder u_1_bit_half_adder_1 (.X(X), .Y(Y), .Sum(n1_bit_half_adder_1_sum), .Cout(n1_bit_half_adder_1_cout));
  _1_bit_half_adder u_1_bit_half_adder_2 (
    .X(n1_bit_half_adder_1_sum), .Y(Cin), .Sum(Sum), .Cout(n1_bit_half_adder_2_cout));
  or or_1 (Cout, n1_bit_half_adder_1_cout, n1_bit_half_adder_2_cout);
endmodule

module _4_bit_adder (
  input  A0,
  input  A1,
  input  A2,
  input  A3,
  input  B0,
  input  B1,
  input  B2,
  input  B3,
  output S0,
  output S1,
  output S2,
  output S3
);

  wire _1_bit_full_adder_2_cout, _1_bit_full_adder_3_cout, _1_bit_full_adder_cout;

  _1_bit_full_adder _1_bit_full_adder (.X(A0), .Y(B0), .Cin(1'b0), .Sum(S0), .Cout(_1_bit_full_adder_cout));
  _1_bit_full_adder _1_bit_full_adder_2 (
    .X(A1), .Y(B1), .Cin(_1_bit_full_adder_cout), .Sum(S1), .Cout(_1_bit_full_adder_2_cout));
  _1_bit_full_adder _1_bit_full_adder_3 (
    .X(A2), .Y(B2), .Cin(_1_bit_full_adder_2_cout), .Sum(S2), .Cout(_1_bit_full_adder_3_cout));
  _1_bit_full_adder _1_bit_full_adder_4 (.X(A3), .Y(B3), .Cin(_1_bit_full_adder_3_cout), .Sum(S3));  // open: Cout
endmodule

module _4_bit_and (
  input  A0,
  input  A1,
  input  A2,
  input  A3,
  input  B0,
  input  B1,
  input  B2,
  input  B3,
  output C0,
  output C1,
  output C2,
  output C3
);

  and and_1 (C0, A0, B0);
  and and_2 (C1, A1, B1);
  and and_3 (C2, A2, B2);
  and and_4 (C3, A3, B3);
endmodule

module _4_bit_or (
  input  A0,
  input  A1,
  input  A2,
  input  A3,
  input  B0,
  input  B1,
  input  B2,
  input  B3,
  output C0,
  output C1,
  output C2,
  output C3
);

  or or_1 (C0, A0, B0);
  or or_2 (C1, A1, B1);
  or or_3 (C2, A2, B2);
  or or_4 (C3, A3, B3);
endmodule

module _4_bit_xor (
  input  A0,
  input  A1,
  input  A2,
  input  A3,
  input  B0,
  input  B1,
  input  B2,
  input  B3,
  output C0,
  output C1,
  output C2,
  output C3
);

  xor xor_1 (C0, A0, B0);
  xor xor_2 (C1, A1, B1);
  xor xor_3 (C2, A2, B2);
  xor xor_4 (C3, A3, B3);
endmodule

module _4_bit_not (
  input  A0,
  input  A1,
  input  A2,
  input  A3,
  output A_prime_0,
  output A_prime_1,
  output A_prime_2,
  output A_prime_3
);

  not not_1 (A_prime_2, A2);
  not not_2 (A_prime_3, A3);
  not not_3 (A_prime_0, A0);
  not not_4 (A_prime_1, A1);
endmodule

module _4_bit_substracter (
  input  A0,
  input  A1,
  input  A2,
  input  A3,
  input  B0,
  input  B1,
  input  B2,
  input  B3,
  output D0,
  output D1,
  output D2,
  output D3
);

  wire _1_bit_full_adder_2_cout, _1_bit_full_adder_3_cout, _1_bit_full_adder_cout, not_1_out, not_2_out,
       not_3_out, not_4_out;

  not not_1 (not_1_out, B0);
  not not_2 (not_2_out, B1);
  not not_3 (not_3_out, B2);
  not not_4 (not_4_out, B3);
  _1_bit_full_adder _1_bit_full_adder (.X(A0), .Y(not_1_out), .Cin(1'b1), .Sum(D0), .Cout(_1_bit_full_adder_cout));
  _1_bit_full_adder _1_bit_full_adder_2 (
    .X(A1), .Y(not_2_out), .Cin(_1_bit_full_adder_cout), .Sum(D1), .Cout(_1_bit_full_adder_2_cout));
  _1_bit_full_adder _1_bit_full_adder_3 (
    .X(A2), .Y(not_3_out), .Cin(_1_bit_full_adder_2_cout), .Sum(D2), .Cout(_1_bit_full_adder_3_cout));
  _1_bit_full_adder _1_bit_full_adder_4 (
    .X(A3), .Y(not_4_out), .Cin(_1_bit_full_adder_3_cout), .Sum(D3));  // open: Cout
endmodule

module _2_to_1_MUX (
  input  I0,
  input  I1,
  input  OP,
  output Z
);

  wire and_1_out, and_2_out, not_1_out;

  and and_1 (and_1_out, I0, not_1_out);
  not not_1 (not_1_out, OP);
  and and_2 (and_2_out, I1, OP);
  or or_1 (Z, and_1_out, and_2_out);
endmodule

module _4_to_1_MUX (
  input  I0,
  input  I1,
  input  I2,
  input  OP1,
  input  I3,
  input  OP0,
  output Z
);

  wire _2_to_1_MUX_2_z, _2_to_1_MUX_z;

  _2_to_1_MUX _2_to_1_MUX (.I0(I0), .I1(I1), .OP(OP0), .Z(_2_to_1_MUX_z));
  _2_to_1_MUX _2_to_1_MUX_2 (.I0(I2), .I1(I3), .OP(OP0), .Z(_2_to_1_MUX_2_z));
  _2_to_1_MUX _2_to_1_MUX_3 (.I0(_2_to_1_MUX_z), .I1(_2_to_1_MUX_2_z), .OP(OP1), .Z(Z));
endmodule

module _8_to_1_MUX (
  input  I0,
  input  I1,
  input  I2,
  input  I3,
  input  I4,
  input  I5,
  input  I6,
  input  I7,
  input  OP0,
  input  OP1,
  input  OP3,
  output Z
);

  wire _4_to_1_MUX_2_z, _4_to_1_MUX_z;

  _4_to_1_MUX _4_to_1_MUX (.I0(I0), .I1(I1), .I2(I2), .I3(I3), .OP0(OP0), .OP1(OP1), .Z(_4_to_1_MUX_z));
  _4_to_1_MUX _4_to_1_MUX_2 (.I0(I4), .I1(I5), .I2(I6), .I3(I7), .OP0(OP0), .OP1(OP1), .Z(_4_to_1_MUX_2_z));
  _2_to_1_MUX _2_to_1_MUX (.I0(_4_to_1_MUX_z), .I1(_4_to_1_MUX_2_z), .OP(OP3), .Z(Z));
endmodule
